// Digital circuit control.dig as structural Verilog
module control (
  input  [4:0] op,
  input  stall,
  input  clock,
  input  skip_n,
  output [2:0] aluop,
  output skip,
  output halt,
  output error,
  output en_write,
  output mem,
  output memop,
  output en_fetch,
  output jump
);

  wire and_3_out, not_1_out;
  wire [0:0] and_1_out;

  and and_1 (and_1_out[0], ~op[3], op[4]);  // And
  and and_2 (jump, ~op[1], op[2], op[3], op[4]);  // And
  and and_3 (and_3_out, op[1], ~op[2], ~op[3], ~op[4], ~en_fetch);  // And
  and and_4 (mem, op[4], op[3], op[2], op[1]);
  Multiplexer #(.Selector_Bits(2), .Bits(3)) multiplexer_1 (
    .sel({mem, and_1_out[0]}), .in_0(3'b111), .in_1(op[2:0]), .in_2(3'b000), .in_3(3'b000), .out(aluop));
  not not_1 (not_1_out, op[0]);
  and and_5 (halt, op[0], and_3_out);
  and and_6 (error, and_3_out, not_1_out);
  Multiplexer multiplexer_2 (.sel(mem), .in_0(1'b0), .in_1(op[0]), .out(memop));
  Register u_skip (.D(skip_n), .C(clock), .en(en_fetch), .Q(skip));
  not not_2 (en_fetch, stall);
  and and_7 (en_write, ~skip, en_fetch);  // And

  // Other names for the same wires on the sheet: en_halt = en_fetch; en_skip = en_fetch

  // Notes on the sheet:
  //   Alu Ops
  //   Branches
  //   Mem Access
  //   Nop Logic
  //   Halt
  //   Halt Logic
  //   Skip Logic
  //   Stall Logic
endmodule

/* Test case ALU Ops:
op      stall aluop jump halt error mem memop
0b10000 0     0     0    0    0     0   0
0b01000 0     7     0    0    0     0   0
0b10011 0     3     0    0    0     0   0
0b01011 0     7     0    0    0     0   0
0b10011 1     3     0    0    0     0   0
*/

/* Test case Halt:
op      stall clock t_in aluop jump halt error mem memop

# with T clear
0b00001 0     0     0    7     0    0    1     0   0

# with T set
0b00001 0     1     1    7     0    1    0     0   0

# reset T
0b00001 0     1     0    7     0    1    0     0   0
0b00001 0     1     0    7     0    1    0     0   0

# check stall
0b00001 1     0     0    7     0    0    0     0   0
0b00001 1     1     1    7     0    0    0     0   0
*/

/* Test case Branches:
op      stall clock t_in aluop jump en_fetch halt error mem memop
0b11100 0     0     0    7     1    1        0    0     0   0

# with T clear
0b11100 0     0     0    7     1    1        0    0     0   0
0b11010 0     0     0    7     0    1        0    0     0   0
0b11011 0     0     0    7     1    1        0    0     0   0

# with T set
0b11100 0     1     1    7     1    1        0    0     0   0
0b11010 0     1     1    7     1    1        0    0     0   0
0b11011 0     1     1    7     0    1        0    0     0   0

# stalled
0b11100 1     0     0    7     1    0        0    0     0   0
0b11010 1     0     0    7     1    0        0    0     0   0
0b11011 1     0     0    7     0    0        0    0     0   0
0b11010 1     1     1    7     1    0        0    0     0   0
0b11011 1     1     1    7     0    0        0    0     0   0
*/

/* Test case Mem Access:
op      stall aluop jump halt error mem memop

0b11110 0     0     0    0    0     1   0
0b11111 0     0     0    0    0     1   1

0b11110 1     0     0    0    0     1   0
0b11111 1     0     0    0    0     1   1
*/
