// Digital circuit decoder.dig as structural Verilog
module decoder (
  input  [15:0] rdval,
  input  [15:0] rsval,
  input  [31:0] instr,
  output [1:0] rs,
  output [1:0] rd,
  output [1:0] result_mux,
  output [15:0] L,
  output [15:0] R,
  output move,
  output add,
  output jump
);

  Multiplexer #(.Bits(16)) multiplexer_1 (.sel(instr[27]), .in_0(instr[15:0]), .in_1(rsval), .out(R));
  Decoder #(.Selector_Bits(3)) decoder_1 (
    .sel(instr[26:24]), .out_0(add), .out_6(move), .out_7(jump));  // open: out_1, out_2, out_3, out_4, out_5
  PriorityEncoder #(.Selector_Bits(2)) priorityencoder_1 (
    .in0(jump), .in1(add), .in2(move), .in3(1'b0), .num(result_mux));  // open: any

  assign L = rdval;
  assign rd = instr[17:16];
  assign rs = instr[21:20];
endmodule
