// Digital circuit execute.dig as structural Verilog
module execute (
  input  [15:0] L,
  input  [15:0] R,
  input  [4:0] op,
  output [15:0] result,
  output halt,
  output error
);

  wire and_1_out, musteq, musteq_eq, not_1_out;
  wire [2:0] multiplexer_1_out;
  wire [15:0] add_1_s;

  and and_1 (and_1_out, ~op[3], op[4]);  // And
  Multiplexer #(.Bits(3)) multiplexer_1 (.sel(and_1_out), .in_0(3'b111), .in_1(op[2:0]), .out(multiplexer_1_out));
  Decoder #(.Selector_Bits(3)) decoder_1 (
    .sel(multiplexer_1_out), .out_5(musteq));  // open: out_0, out_1, out_2, out_3, out_4, out_6, out_7
  Add #(.Bits(16)) add_1 (.a(L), .b(R), .c_i(1'b0), .s(add_1_s));  // open: c_o
  Comparator #(.Bits(16)) u_musteq (.a(R), .b(L), .eq(musteq_eq));  // open: gt, lt
  and and_2 (halt, musteq_eq, musteq);
  and and_3 (error, musteq, not_1_out);
  not not_1 (not_1_out, musteq_eq);
  Multiplexer #(.Selector_Bits(3), .Bits(16)) multiplexer_2 (
    .sel(multiplexer_1_out), .in_0(add_1_s), .in_1({16{1'b0}}), .in_2({16{1'b0}}), .in_3({16{1'b0}}),
    .in_4({16{1'b0}}), .in_5(L), .in_6(R), .in_7(L), .out(result));
endmodule
