// Digital circuit fetch.dig as structural Verilog
module fetch (
  input  [15:0] instr_i,
  input  clock,
  input  [15:0] value,
  input  jump,
  output [3:0] pc,
  output [15:0] instr_o
);

  CounterPreset #(.Bits(4), .isProgramCounter("true")) u_PC (
    .en(1'b1), .C(clock), .dir(1'b0), .in(value[3:0]), .ld(jump), .clr(1'b0), .out(pc));  // open: ovf

  assign instr_o = instr_i;
endmodule
